# Fritzing sketch Thermostat with display (saved by Fritzing 0.9.10b)
breadboards: 1

parts:
  OLED_I2C1 = OLED 128x64 I2C Monochrome Display
  Mod1 = Amica NodeMCU DEVKIT 1.0
  Part1 = BME280 Breakout  # not connected
  S1 = Pushbutton [package=THT]

nets:
  N1: OLED_I2C1.SDA, Mod1.pin_13
  N2: OLED_I2C1.SCK, Mod1.pin_14
  N3: OLED_I2C1.VDD, Mod1.pin1, Mod1.pin_10, S1.leg0
  N4: OLED_I2C1.GND, Mod1.pin2, Mod1.pin_9
  N5: Mod1.pin8, S1.leg1
